// Logisim project B2_Group2_offline1.circ as structural Verilog: 1 circuit, main circuit main
module main (
  input  [3:0] A,
  input  [3:0] B,
  input  Cs0,
  input  Cs1,
  input  Cs2,
  output C4,
  output C1,
  output GARBAGE,
  output C3,
  output GARBAGE_2,
  output C2,
  output V,
  output Z,
  output S,
  output C,
  output Cout,
  output S3,
  output S2,
  output S1,
  output S0
);

  wire n7404_1_p2, n7404_1_p3, n7404_1_p4, n7404_1_p6, n7404_1_p9, n7404_1_p11, n7404_1_p13, n7404_2_p3,
       n7408_1_p2, n7408_1_p8, n7408_2_p3, n7408_3_p6, n7408_3_p11, n7408_3_p14, n7432_1_p2, n7432_1_p5,
       n7432_1_p9, n7432_1_p11, n7432_1_p12, n7432_1_p14, n7432_2_p3, n7432_2_p6, n7432_3_p2, n7432_3_p5,
       n7432_3_p10, n7432_3_p12, n7432_3_p13, n7483_1_p1, n7483_1_p2, n7483_1_p7, n7483_1_p11, n7483_1_p13,
       n7483_2_p1, n7483_2_p7, n7483_2_p8, n7483_2_p11;

  // _7408 7408_1: pin names not known; wires that end beside it: C4, n7408_1_p2, C, 1'b0, 1'b1, C3, n7408_1_p2, n7408_1_p8
  // _7404 7404_1: pin names not known; wires that end beside it: Cs0, n7404_1_p2, n7404_1_p3, n7404_1_p4, B[3], n7404_1_p6, 1'b0, B[0], n7404_1_p9, B[1], n7404_1_p11, B[2], n7404_1_p13
  // _7486 7486_1: pin names not known; wires that end beside it: Cs0, Cs1, n7404_1_p3, C, n7408_1_p8, V, 1'b0, 1'b1
  // _7404 7404_2: pin names not known; wires that end beside it: Cs1, n7408_1_p2, n7404_2_p3, Z, 1'b0, 1'b1
  // _7483 7483_1: pin names not known; wires that end beside it: n7483_1_p1, n7483_1_p2, S, GARBAGE_2, C4, 1'b1, n7483_1_p7, n7408_1_p8, 1'b0, 1'b1, n7483_1_p11, C3, n7483_1_p13, 1'b0, S2, 1'b0
  // _7432 7432_1: pin names not known; wires that end beside it: A[2], n7432_1_p2, n7483_1_p13, A[3], n7432_1_p5, n7483_1_p2, 1'b0, 1'b1, n7432_1_p9, A[0], n7432_1_p11, n7432_1_p12, A[1], n7432_1_p14
  // _7432 7432_2: pin names not known; wires that end beside it: S, S2, n7432_2_p3, n7432_2_p3, S1, n7432_2_p6, 1'b0, 1'b1, S0, n7432_2_p6, n7404_2_p3
  // _7408 7408_2: pin names not known; wires that end beside it: n7404_1_p2, Cs1, n7408_2_p3, n7408_2_p3, n7404_1_p9, n7432_1_p9, 1'b0, 1'b1, n7404_1_p13, n7408_2_p3, n7432_1_p2, n7404_1_p11, n7408_2_p3, n7432_1_p12
  // _7483 7483_2: pin names not known; wires that end beside it: n7483_2_p1, n7432_1_p14, S1, GARBAGE, C2, 1'b1, n7483_2_p7, n7483_2_p8, 1'b0, 1'b1, n7483_2_p11, C1, n7432_1_p11, 1'b0, S0, 1'b0
  // _7408 7408_3: pin names not known; wires that end beside it: n7408_2_p3, n7404_1_p6, n7432_1_p5, Cs1, n7404_1_p9, n7408_3_p6, 1'b0, 1'b1, Cs1, n7404_1_p11, n7408_3_p11, Cs1, n7404_1_p13, n7408_3_p14
  // _7432 7432_3: pin names not known; wires that end beside it: n7408_3_p6, n7432_3_p2, n7483_2_p11, n7408_3_p11, n7432_3_p5, n7483_2_p1, 1'b0, 1'b1, n7408_3_p14, n7432_3_p10, n7483_1_p11, n7432_3_p12, n7432_3_p13, n7483_1_p1
  // _7408 7408_4: pin names not known; wires that end beside it: n7404_1_p6, Cs1, n7432_3_p12, n7404_1_p4, B[0], n7432_3_p2, 1'b0, 1'b1, B[2], n7404_1_p4, n7432_3_p10, B[1], n7404_1_p4, n7432_3_p5
  // _7408 7408_5: pin names not known; wires that end beside it: n7404_1_p4, B[3], n7432_3_p13, n7408_1_p2, Cs2, n7483_2_p7, 1'b0, 1'b1, C2, n7408_1_p2, n7483_1_p7, n7408_1_p2, C1, n7483_2_p8

  assign Cout = C;
  assign S3 = S;

  // Notes on the sheet:
  //   CS1 XNOR CS0
  //   X3
  //   X2
  //   X0
  //   X1
  //   B0'CS1CS0'
  //   B1'CS1CS0'
  //   B2'CS1CS0'
  //   B3'CS1CS0'
  //   Y0
  //   Y1
  //   Y2
  //   Y3
  //   B0'CS1
  //   B1'CS1
  //   B2'CS1
  //   B3'CS1
  //   Cin
endmodule
