// Logisim project 10bitMUX.circ as structural Verilog: 1 circuit, main circuit main
module main (
  input  S,
  input  [9:0] A,
  input  [9:0] B,
  output [9:0] Output
);

  // _74157 74157_1: pin names not known; wires that end beside it: S, A[8], B[8], Output[8], 1'b1, 1'b0, A[9], B[9], Output[9]
  // _74157 74157_2: pin names not known; wires that end beside it: S, A[0], B[0], Output[0], A[1], B[1], Output[1], 1'b1, 1'b0, A[2], B[2], Output[2], A[3], B[3], Output[3]
  // _74157 74157_3: pin names not known; wires that end beside it: S, A[4], B[4], Output[4], A[5], B[5], Output[5], 1'b1, 1'b0, A[6], B[6], Output[6], A[7], B[7], Output[7]
endmodule
