// Logisim project 24bitMUX.circ as structural Verilog: 1 circuit, main circuit main
module main (
  input  S,
  input  G,
  input  VCC,
  input  [23:0] in_4,
  input  [23:0] in_5,
  output [23:0] out_6
);

  // _74157 74157_1: pin names not known; wires that end beside it: in_5[12], S, in_4[12], in_5[12], out_6[12], in_4[13], in_5[13], out_6[13], VCC, G, in_4[14], in_5[14], out_6[14], in_4[15], in_5[15], out_6[15]
  // _74157 74157_2: pin names not known; wires that end beside it: S, in_4[0], in_5[0], out_6[0], in_4[1], in_5[1], out_6[1], VCC, G, in_4[2], in_5[2], out_6[2], in_4[3], in_5[3], out_6[3]
  // _74157 74157_3: pin names not known; wires that end beside it: S, in_4[4], in_5[4], out_6[4], in_4[5], in_5[5], out_6[5], VCC, G, in_4[6], in_5[6], out_6[6], in_4[7], in_5[7], out_6[7]
  // _74157 74157_4: pin names not known; wires that end beside it: S, in_4[16], in_5[16], out_6[16], in_4[17], in_5[17], out_6[17], VCC, G, in_4[18], in_5[18], out_6[18], in_4[19], in_5[19], out_6[19], out_6[19], out_6[20]
  // _74157 74157_5: pin names not known; wires that end beside it: S, in_4[8], in_5[8], out_6[8], in_4[9], in_5[9], out_6[9], VCC, G, in_4[10], in_5[10], out_6[10], in_4[11], in_5[11], out_6[11]
  // _74157 74157_6: pin names not known; wires that end beside it: S, in_4[20], in_5[20], out_6[20], in_4[21], in_5[21], out_6[21], VCC, G, in_4[22], in_5[22], out_6[22], in_4[23], in_5[23], out_6[23], out_6[14]
endmodule
