// Logisim project 32bit_mux.circ as structural Verilog: 1 circuit, main circuit main
module main (
  input  G,
  input  Vcc,
  input  S,
  input  [31:0] A,
  input  [31:0] B,
  input  GND,
  output [31:0] Y
);

  // _74157 74157_1: pin names not known; wires that end beside it: S, A[0], B[0], Y[0], A[1], B[1], Y[1], GND, Vcc, G, A[3], B[3], Y[3], A[2], B[2], Y[2]
  // _74157 74157_2: pin names not known; wires that end beside it: S, A[20], B[20], Y[20], A[21], B[21], Y[21], GND, Vcc, G, A[23], B[23], Y[23], A[22], B[22], Y[22]
  // _74157 74157_3: pin names not known; wires that end beside it: S, A[4], B[4], Y[4], A[5], B[5], Y[5], GND, G, G, A[7], B[7], Y[7], A[6], B[6], Y[6]
  // _74157 74157_4: pin names not known; wires that end beside it: S, A[8], B[8], Y[8], A[9], B[9], Y[9], GND, Vcc, G, A[11], B[11], Y[11], A[10], B[10], Y[10]
  // _74157 74157_5: pin names not known; wires that end beside it: S, A[24], B[24], Y[24], A[25], B[25], Y[25], GND, Vcc, G, A[27], B[27], Y[27], A[26], B[26], Y[26]
  // _74157 74157_6: pin names not known; wires that end beside it: S, A[12], B[12], Y[12], A[13], B[13], Y[13], GND, Vcc, G, A[15], B[15], Y[15], A[14], B[14], Y[14]
  // _74157 74157_7: pin names not known; wires that end beside it: S, A[28], B[28], Y[28], A[29], B[29], Y[29], GND, Vcc, G, A[31], B[31], Y[31], A[30], B[30], Y[30]
  // _74157 74157_8: pin names not known; wires that end beside it: S, A[16], B[16], Y[16], A[17], B[17], Y[17], GND, Vcc, G, A[19], B[19], Y[19], A[18], B[18], Y[18]
endmodule
