// Logisim project Floating point offline2.circ as structural Verilog: 8 circuits, main circuit 0.Main
module _1_Floating_point_main (
  input  [31:0] Number_A,
  input  [31:0] Number_B,
  output Output_sign,
  output [31:0] Output_Significand,
  output equal_expononet,
  output Overflow,
  output underflow,
  output [9:0] Output_exponent,
  output [31:0] Output_result
);

  wire comparator_1_eq, comparator_2_eq, n7408_1_p3;
  wire [9:0] Alignment_and_shifting_larger_exp, Normalization_normalized_expo;
  wire [23:0] Alignment_and_shifting_fraction_bit_a_2, Alignment_and_shifting_fraction_shifted;
  wire [31:0] _32_bit_Adder_output_significand, Normalization_normalized_frac, Rounding_output_significand;

  Comparator #(.width(32), .mode("unsigned")) comparator_1 (
    .a(Number_B), .b({32{1'b0}}), .eq(comparator_1_eq));  // open: gt, lt
  Comparator #(.width(32), .mode("unsigned")) comparator_2 (
    .a(Number_A), .b({32{1'b0}}), .eq(comparator_2_eq));  // open: gt, lt
  _2__Allignment Alignment_and_shifting (
    .Fraction_Bit_A(Number_A[20:0]), .Fraction_Bit_B(Number_B[20:0]), .Exp_Bit_A(Number_A[30:21]),
    .Exp_Bit_B(Number_B[30:21]), .Sign_Bit_A(Number_A[31]), .Sign_Bit_B(Number_B[31]),
    .Equal_exponent(equal_expononet), .Fraction_Bit_A_2(Alignment_and_shifting_fraction_bit_a_2),
    .Fraction_Shifted(Alignment_and_shifting_fraction_shifted),
    .Larger_Exp(Alignment_and_shifting_larger_exp), .Output_sign(Output_sign));  // open: out_10, Exp_difference
  _5_Adder _32_bit_Adder (
    .sign_bit_A(Number_A[31]), .sign_bit_B(Number_B[31]),
    .Significand_A(Alignment_and_shifting_fraction_bit_a_2),
    .Significand_B(Alignment_and_shifting_fraction_shifted),
    .Output_significand(_32_bit_Adder_output_significand));  // open: out_6, out_7
  // _7408 7408_1: pin names not known; wires that end beside it: comparator_1_eq, comparator_2_eq, n7408_1_p3
  _6_Normalization Normalization (
    .Input_Significand(_32_bit_Adder_output_significand), .Input_Exponent(Alignment_and_shifting_larger_exp),
    .Normalized_frac(Normalization_normalized_frac), .Normalized_expo(Normalization_normalized_expo));  // open: overflow, undeflow, _29__Position, Position, present
  _7_Rounding Rounding (
    .Output_Significand(Rounding_output_significand), .Input_significand(Normalization_normalized_frac));
  _6_Normalization Normalization_2 (
    .Input_Significand(Rounding_output_significand), .Input_Exponent(Normalization_normalized_expo),
    .overflow(Overflow), .undeflow(underflow), .Normalized_frac(Output_Significand),
    .Normalized_expo(Output_exponent));  // open: _29__Position, Position, present
  _32bit_mux_main _32_bit_mux (
    .G(1'b0), .S(n7408_1_p3), .A({Output_sign, Output_exponent, Output_Significand[28:8]}), .B({32{1'b0}}),
    .Y(Output_result));  // open: GND, Vcc

  // Notes on the sheet:
  //   sign
  //   sign
  //   fraction 21bits
  //   exp 10bits
  //   fraction 21bits
  //   exp 10bits
endmodule

module _2__Allignment (
  input  [20:0] Fraction_Bit_A,
  input  [20:0] Fraction_Bit_B,
  input  [9:0] Exp_Bit_A,
  input  [9:0] Exp_Bit_B,
  input  Sign_Bit_A,
  input  Sign_Bit_B,
  output [23:0] Fraction_Bit_A_2,
  output [23:0] Fraction_Shifted,
  output [9:0] Exp_difference,
  output out_10,
  output [9:0] Larger_Exp,
  output Output_sign,
  output Equal_exponent
);

  wire comparator_1_gt, comparator_1_lt, n7404_1_p2, n74157_1_p4, n74157_1_p7;
  wire [9:0] main_3_output;
  wire [23:0] main_1_out_6;

  _24bitMUX_main main_1 (
    .S(comparator_1_gt), .G(1'b0), .VCC(1'b1), .in_4({3'b001, Fraction_Bit_A}),
    .in_5({3'b001, Fraction_Bit_B}), .out_6(main_1_out_6));
  _24bitMUX_main main_2 (
    .S(n7404_1_p2), .G(1'b0), .VCC(1'b1), .in_4({3'b001, Fraction_Bit_A}), .in_5({3'b001, Fraction_Bit_B}),
    .out_6(Fraction_Bit_A_2));
  _10bitMUX_main main_3 (.S(comparator_1_gt), .A(Exp_Bit_A), .B(Exp_Bit_B), .Output(main_3_output));
  Comparator #(.width(10), .mode("unsigned")) comparator_1 (
    .a(Exp_Bit_A), .b(Exp_Bit_B), .gt(comparator_1_gt), .eq(Equal_exponent), .lt(comparator_1_lt));
  _10bitMUX_main main_4 (.S(comparator_1_lt), .A(Exp_Bit_A), .B(Exp_Bit_B), .Output(Larger_Exp));
  // _74157 74157_1: pin names not known; wires that end beside it: comparator_1_gt, Sign_Bit_A, Sign_Bit_B, n74157_1_p4, Sign_Bit_B, Sign_Bit_A, n74157_1_p7, 1'b0, 1'b1, 1'b0
  // _7404 7404_1: pin names not known; wires that end beside it: comparator_1_gt, n7404_1_p2
  Subtractor #(.width(10)) subtractor_1 (
    .a(Larger_Exp), .b(main_3_output), .out(Exp_difference), .bin(1'b0), .bout(out_10));
  _3_Shifter u_3_shifter_1 (
    .significand(main_1_out_6), .Exp_difference(Exp_difference), .Fraction_Shifted(Fraction_Shifted));
  _4_Sign_Bit_Decider u_4_sign_bit_decider_1 (
    .sign_Bit_A(n74157_1_p4), .sign_bit_B(n74157_1_p7), .Significand_A(Fraction_Shifted),
    .Significand_B(Fraction_Bit_A_2), .output_sign(Output_sign));

  // Notes on the sheet:
  //   24 bit mux
  //   24 bit mux
  //   10Bit mux
  //   10 bit Comparator
  //   if A>B
  //   if A<B
  //   10 bit mux
  //   10 bit subtractor
  //   sign bit decider
  //   shifter
endmodule

module _3_Shifter (
  input  [23:0] significand,
  input  [9:0] Exp_difference,
  output [23:0] Fraction_Shifted
);

  wire comparator_1_gt;
  wire [4:0] bit_extender_1_out;
  wire [23:0] shifter_1_out;

  Bit_Extender #(.in_width(10), .out_width(5)) bit_extender_1 (.in(Exp_difference), .out(bit_extender_1_out));
  Shifter #(.width(24), .shift("lr")) shifter_1 (.in(significand), .\dist (bit_extender_1_out), .out(shifter_1_out));
  Comparator #(.width(10), .mode("unsigned")) comparator_1 (
    .a(Exp_difference), .b(10'h1f), .gt(comparator_1_gt));  // open: eq, lt
  _24bitMUX_main main_1 (
    .S(comparator_1_gt), .G(1'b0), .VCC(1'b1), .in_4(shifter_1_out), .in_5({24{1'b0}}),
    .out_6(Fraction_Shifted));

  // Notes on the sheet:
  //   (31)decimal 
  //   Shifter
  //   Comparator
  //   A
  //   24 bit mux
  //   B
endmodule

module _4_Sign_Bit_Decider (
  input  sign_Bit_A,
  input  sign_bit_B,
  input  [23:0] Significand_A,
  input  [23:0] Significand_B,
  output output_sign
);

  wire comparator_1_eq, comparator_1_gt, n7408_1_p3, n74157_1_p1, n74157_1_p4;

  Comparator #(.width(24), .mode("unsigned")) comparator_1 (
    .a(Significand_A), .b(Significand_B), .gt(comparator_1_gt), .eq(comparator_1_eq));  // open: lt
  // _74157 74157_1: pin names not known; wires that end beside it: n74157_1_p1, sign_Bit_A, sign_bit_B, n74157_1_p4, 1'b0
  // _7404 7404_1: pin names not known; wires that end beside it: comparator_1_gt, n74157_1_p1
  // _7408 7408_1: pin names not known; wires that end beside it: sign_Bit_A, sign_bit_B, n7408_1_p3
  // _74157 74157_2: pin names not known; wires that end beside it: comparator_1_eq, n74157_1_p4, n7408_1_p3, output_sign, 1'b0

  // Notes on the sheet:
  //   comparator
  //   larger's sign
endmodule

module _5_Adder (
  input  sign_bit_A,
  input  sign_bit_B,
  input  [23:0] Significand_A,
  input  [23:0] Significand_B,
  output [31:0] Output_significand,
  output out_6,
  output out_7
);

  wire comparator_1_gt, n7404_1_p2, n7486_1_p3;
  wire [31:0] adder_1_out, main_1_y, main_3_y, subtractor_1_out;

  // _7486 7486_1: pin names not known; wires that end beside it: sign_bit_A, sign_bit_B, n7486_1_p3, 1'b0, 1'b1
  Adder #(.width(32)) adder_1 (
    .a({Significand_A, {8{1'b0}}}), .b({Significand_B, {8{1'b0}}}), .out(adder_1_out), .cin(1'b0),
    .cout(out_6));
  _32bit_mux_main main_1 (
    .G(1'b0), .S(comparator_1_gt), .A({Significand_A, {8{1'b0}}}), .B({Significand_B, {8{1'b0}}}),
    .GND(1'b0), .Vcc(1'b1), .Y(main_1_y));
  Comparator #(.width(32), .mode("unsigned")) comparator_1 (
    .a({Significand_A, {8{1'b0}}}), .b({Significand_B, {8{1'b0}}}), .gt(comparator_1_gt));  // open: eq, lt
  _32bit_mux_main main_2 (
    .G(1'b0), .S(n7486_1_p3), .A(adder_1_out), .B(subtractor_1_out), .Vcc(1'b1), .Y(Output_significand));  // open: GND
  _32bit_mux_main main_3 (
    .G(1'b0), .S(n7404_1_p2), .A({Significand_A, {8{1'b0}}}), .B({Significand_B, {8{1'b0}}}), .GND(1'b0),
    .Vcc(1'b1), .Y(main_3_y));
  // _7404 7404_1: pin names not known; wires that end beside it: comparator_1_gt, n7404_1_p2
  Subtractor #(.width(32)) subtractor_1 (.a(main_3_y), .b(main_1_y), .out(subtractor_1_out), .bin(1'b0), .bout(out_7));

  // Notes on the sheet:
  //   32 bit mux
  //   comparator
  //   32bit mux
  //   32 bit mux
endmodule

module _6_Normalization (
  input  [31:0] Input_Significand,
  input  [9:0] Input_Exponent,
  output [4:0] _29__Position,
  output [4:0] Position,
  output [31:0] Normalized_frac,
  output present,
  output [9:0] Normalized_expo,
  output undeflow,
  output overflow
);

  wire comparator_1_eq, comparator_1_lt, comparator_2_eq, comparator_2_lt;
  wire [9:0] adder_1_out, bit_extender_1_out, main_2_output, subtractor_2_out;
  wire [31:0] _32_bit_mux_2_y, shifter_1_out, shifter_2_out;

  BitFinder #(.width(32), .\type ("high1")) bitfinder_1 (.in(Input_Significand), .index(Position), .found(present));
  Subtractor #(.width(5)) subtractor_1 (.a(5'b11101), .b(Position), .out(_29__Position));  // open: bin, bout
  Comparator #(.width(5), .mode("unsigned")) comparator_1 (
    .a(Position), .b(5'b11101), .eq(comparator_1_eq), .lt(comparator_1_lt));  // open: gt
  Shifter #(.width(32), .shift("lr")) shifter_1 (.in(Input_Significand), .\dist (5'b00001), .out(shifter_1_out));
  _10bitMUX_main main_1 (.S(comparator_1_eq), .A(main_2_output), .B(Input_Exponent), .Output(Normalized_expo));
  _32bit_mux_main _32_bit_mux (
    .G(1'b0), .S(comparator_1_eq), .A(_32_bit_mux_2_y), .B(Input_Significand), .Vcc(1'b1), .Y(Normalized_frac));  // open: GND
  Shifter #(.width(32)) shifter_2 (.in(Input_Significand), .\dist (_29__Position), .out(shifter_2_out));
  assign bit_extender_1_out = {{5{1'b0}}, _29__Position};  // Bit_Extender bit_extender_1
  _32bit_mux_main _32_bit_mux_2 (
    .G(1'b0), .S(comparator_1_lt), .A(shifter_1_out), .B(shifter_2_out), .Vcc(1'b1), .Y(_32_bit_mux_2_y));  // open: GND
  Adder #(.width(10)) adder_1 (.a(Input_Exponent), .b(10'h1), .out(adder_1_out), .cin(1'b0));  // open: cout
  Subtractor #(.width(10)) subtractor_2 (
    .a(Input_Exponent), .b(bit_extender_1_out), .out(subtractor_2_out), .bin(1'b0));  // open: bout
  _10bitMUX_main main_2 (.S(comparator_1_lt), .A(adder_1_out), .B(subtractor_2_out), .Output(main_2_output));
  Comparator #(.width(10), .mode("unsigned")) comparator_2 (
    .a(Normalized_expo), .b({10{1'b0}}), .eq(comparator_2_eq), .lt(comparator_2_lt));  // open: gt
  Comparator #(.width(10), .mode("unsigned")) comparator_3 (
    .a(Normalized_expo), .b(10'h3fe), .gt(overflow));  // open: eq, lt
  // _7432 7432_1: pin names not known; wires that end beside it: comparator_2_eq, comparator_2_lt, undeflow
endmodule

module _7_Rounding (
  input  [31:0] Input_significand,
  output [31:0] Output_Significand
);

  wire n7432_1_p3, n7432_1_p6, n7432_1_p9, n7432_1_p12, n7432_2_p1, n7432_2_p2, n7432_2_p3, n7432_2_p5,
       n7432_2_p9;
  wire [8:8] n7432_2_p6;

  // _7432 7432_1: pin names not known; wires that end beside it: Input_significand[5], Input_significand[4], n7432_1_p3, n7432_1_p3, Input_significand[3], n7432_1_p6, Input_significand[2], n7432_1_p6, n7432_1_p9, n7432_1_p9, Input_significand[1], n7432_1_p12
  // _7432 7432_2: pin names not known; wires that end beside it: n7432_2_p1, n7432_2_p2, n7432_2_p3, n7432_2_p3, n7432_2_p5, n7432_2_p6[8], n7432_1_p12, Input_significand[0], n7432_2_p9
  // _7408 7408_1: pin names not known; wires that end beside it: Input_significand[7], Input_significand[6], n7432_2_p2, Input_significand[7], n7432_2_p9, n7432_2_p1, Input_significand[7], Input_significand[8], n7432_2_p5
  Adder #(.width(32)) adder_1 (
    .a(Input_significand), .b({{23{1'b0}}, n7432_2_p6[8], {8{1'b0}}}), .out(Output_Significand), .cin(1'b0));  // open: cout

  // Notes on the sheet:
  //   P
  //   G
  //   R
  //   S
  //   GR
  //   GS
  //   GR+GS+GP
  //   GP
endmodule

module _0_Main (
  input  [31:0] Number_A,
  input  [31:0] Number_B,
  output [31:0] Output,
  output Underflow,
  output Overflow
);

  _1_Floating_point_main Floating_Point (
    .Number_A(Number_A), .Number_B(Number_B), .Overflow(Overflow), .underflow(Underflow),
    .Output_result(Output));  // open: Output_Significand, Output_exponent, Output_sign, equal_expononet

  // Notes on the sheet:
  //   (5)    50+ 0.49= 50.49
endmodule
