// Logisim project B2_GROUP2.circ as structural Verilog: 6 circuits, main circuit main
module main (
  input  CLR,
  output [7:0] PC,
  output [3:0] zero,
  output [3:0] t0,
  output [3:0] t4,
  output [3:0] t1,
  output [3:0] t2,
  output [3:0] t3
);

  wire alu2_1_zf, and_1_out, and_2_out, clock_1_out, control_1_alu_src, control_1_beq, control_1_bneq,
       control_1_jump, control_1_memread, control_1_memtoreg, control_1_memwrite, control_1_rdst,
       control_1_registerwrite, not_1_out, or_1_out;
  wire [2:0] control_1_aluop;
  wire [3:0] alu2_1_result, multiplexer_1_out, multiplexer_3_out, multiplexer_5_out, ram_1_data,
       registers_1_read_data_1, registers_1_read_data_2;
  wire [7:0] adder_1_out, adder_2_out, multiplexer_2_out, multiplexer_4_out, multiplexer_6_out;
  wire [15:0] rom_1_data;

  Register #(.trigger("falling")) register_1 (.D(multiplexer_6_out), .Q(PC), .clk(clock_1_out), .clr(CLR));  // open: en
  Adder adder_1 (.a(PC), .b(8'h1), .out(adder_1_out));  // open: cin, cout
  ROM #(.dataWidth(16)) rom_1 (.addr(PC), .data(rom_1_data));  // open: sel
  Clock clock_1 (.out(clock_1_out));
  control control_1 (
    .Opcode(rom_1_data[15:12]), .RegisterWrite(control_1_registerwrite), .ALU_SRC(control_1_alu_src),
    .MemWrite(control_1_memwrite), .ALUOP(control_1_aluop), .MemToReG(control_1_memtoreg),
    .MemRead(control_1_memread), .Bneq(control_1_bneq), .Beq(control_1_beq), .Jump(control_1_jump),
    .RDst(control_1_rdst));
  Multiplexer #(.width(4), .enable("false")) multiplexer_1 (
    .in0(rom_1_data[7:4]), .in1(rom_1_data[3:0]), .out(multiplexer_1_out), .sel(control_1_rdst));
  registers registers_1 (
    .Read_Address_1(rom_1_data[11:8]), .Read_Address_2(rom_1_data[7:4]), .RegWrite(control_1_registerwrite),
    .Clk(clock_1_out), .Write_Address(multiplexer_1_out), .Write_Data(multiplexer_5_out),
    .Read_Data_1(registers_1_read_data_1), .Read_Data_2(registers_1_read_data_2), .zero(zero), .t0(t0),
    .t1(t1), .t2(t2), .t3(t3), .t4(t4), .CLR(CLR));
  Multiplexer #(.width(8), .enable("false")) multiplexer_2 (
    .in0({4'b0000, rom_1_data[3:0]}), .in1({4'b1111, rom_1_data[3:0]}), .out(multiplexer_2_out),
    .sel(rom_1_data[3]));
  Multiplexer #(.width(4), .enable("false")) multiplexer_3 (
    .in0(registers_1_read_data_2), .in1(rom_1_data[3:0]), .out(multiplexer_3_out), .sel(control_1_alu_src));
  ALU2 alu2_1 (
    .A(registers_1_read_data_1), .B(multiplexer_3_out), .ALUOP(control_1_aluop), .Result(alu2_1_result),
    .ZF(alu2_1_zf));  // open: OVERFLOW
  Adder adder_2 (.a(PC), .b(multiplexer_2_out), .out(adder_2_out));  // open: cin, cout
  and and_1 (and_1_out, control_1_beq, alu2_1_zf);
  not not_1 (not_1_out, alu2_1_zf);
  and and_2 (and_2_out, control_1_bneq, not_1_out);
  RAM #(.addrWidth(4), .dataWidth(4), .bus("separate")) ram_1 (
    .addr(alu2_1_result), .din(registers_1_read_data_2), .data(ram_1_data), .str(control_1_memwrite),
    .clk(clock_1_out), .ld(control_1_memread), .clr(CLR));  // open: sel
  or or_1 (or_1_out, and_1_out, and_2_out);
  Multiplexer #(.width(8), .enable("false")) multiplexer_4 (
    .in0(adder_1_out), .in1(adder_2_out), .out(multiplexer_4_out), .sel(or_1_out));
  Multiplexer #(.width(4), .enable("false")) multiplexer_5 (
    .in0(alu2_1_result), .in1(ram_1_data), .out(multiplexer_5_out), .sel(control_1_memtoreg));
  Multiplexer #(.width(8), .enable("false")) multiplexer_6 (
    .in0(multiplexer_4_out), .in1(rom_1_data[11:4]), .out(multiplexer_6_out), .sel(control_1_jump));

  // Notes on the sheet:
  //   contents of rom_1 (hex, n*v repeats v):
  //   d713 772e f120 2123 24 8213 e221 5322 9150 3331 4224 9110 c020 6421 1115 b241 9120 a20b
endmodule

module registers (
  input  [3:0] Read_Address_1,
  input  [3:0] Read_Address_2,
  input  RegWrite,
  input  Clk,
  input  [3:0] Write_Address,
  input  [3:0] Write_Data,
  input  CLR,
  output [3:0] zero,
  output [3:0] t0,
  output [3:0] Read_Data_1,
  output [3:0] t1,
  output [3:0] t2,
  output [3:0] t3,
  output [3:0] t4,
  output [3:0] Read_Data_2
);

  wire and_1_out, demultiplexer_1_out0, demultiplexer_1_out1, demultiplexer_1_out2, demultiplexer_1_out3,
       demultiplexer_1_out4;

  Demultiplexer #(.select(3), .enable("false")) demultiplexer_1 (
    .out0(demultiplexer_1_out0), .out1(demultiplexer_1_out1), .out2(demultiplexer_1_out2),
    .out3(demultiplexer_1_out3), .out4(demultiplexer_1_out4), .in(and_1_out), .sel(Write_Address[2:0]));  // open: out5, out6, out7
  and and_1 (and_1_out, RegWrite, Clk);
  Register #(.width(4)) u_zero (.D(4'b0000), .Q(zero), .clk(1'b0));  // open: en, clr
  Register #(.width(4)) u_t0 (.D(Write_Data), .Q(t0), .clk(demultiplexer_1_out0), .clr(CLR));  // open: en
  Register #(.width(4)) u_t1 (.D(Write_Data), .Q(t1), .clk(demultiplexer_1_out1), .clr(CLR));  // open: en
  Register #(.width(4)) u_t2 (.D(Write_Data), .Q(t2), .clk(demultiplexer_1_out2), .clr(CLR));  // open: en
  Register #(.width(4)) u_t3 (.D(Write_Data), .Q(t3), .clk(demultiplexer_1_out3), .clr(CLR));  // open: en
  Register #(.width(4)) u_t4 (.D(Write_Data), .Q(t4), .clk(demultiplexer_1_out4), .clr(CLR));  // open: en
  Multiplexer #(.select(3), .width(4), .disabled(0), .enable("false")) multiplexer_1 (
    .in0(t0), .in1(t1), .in2(t2), .in3(t3), .in4(t4), .in5(4'b0000), .in6(4'b0000), .in7(zero),
    .out(Read_Data_1), .sel(Read_Address_1[2:0]));
  Multiplexer #(.select(3), .width(4), .disabled(0), .enable("false")) multiplexer_2 (
    .in0(t0), .in1(t1), .in2(t2), .in3(t3), .in4(t4), .in5(4'b0000), .in6(4'b0000), .in7(zero),
    .out(Read_Data_2), .sel(Read_Address_2[2:0]));
endmodule

module control (
  input  [3:0] Opcode,
  output RegisterWrite,
  output ALU_SRC,
  output MemWrite,
  output [2:0] ALUOP,
  output MemToReG,
  output MemRead,
  output Bneq,
  output Beq,
  output Jump,
  output RDst
);

  ROM #(.addrWidth(4), .dataWidth(12)) rom_1 (
    .addr(Opcode), .data({RDst, Jump, Beq, Bneq, MemRead, MemToReG, ALUOP, MemWrite, ALU_SRC, RegisterWrite}));  // open: sel

  // Notes on the sheet:
  //   contents of rom_1 (hex, n*v repeats v):
  //   821 13 809 2b c3 208 1b b 6 400 108 819 811 3 33 801
endmodule

module ALU2 (
  input  [3:0] A,
  input  [3:0] B,
  input  [2:0] ALUOP,
  output OVERFLOW,
  output [3:0] Result,
  output ZF
);

  wire add_1_overflow, sub_1_overflow;
  wire [3:0] add_1_result, AND_out, NOR_out, or_out, shifter_1_out, shifter_2_out, sub_1_result;

  add add_1 (.A(A), .B(B), .Result(add_1_result), .OVERFLOW(add_1_overflow));
  sub sub_1 (.A(A), .B(B), .result(sub_1_result), .overflow(sub_1_overflow));
  assign or_out = A | B;  // OR_Gate or, 4 bits wide
  assign AND_out = A & B;  // AND_Gate AND, 4 bits wide
  assign NOR_out = ~(A | B);  // NOR_Gate NOR, 4 bits wide
  Shifter #(.width(4)) shifter_1 (.in(A), .\dist (B[1:0]), .out(shifter_1_out));
  Shifter #(.width(4), .shift("lr")) shifter_2 (.in(A), .\dist (B[1:0]), .out(shifter_2_out));
  Multiplexer #(.select(3), .width(4), .enable("false")) multiplexer_1 (
    .in0(add_1_result), .in1(sub_1_result), .in2(or_out), .in3(AND_out), .in4(NOR_out), .in5(shifter_1_out),
    .in6(shifter_2_out), .in7(4'b0000), .out(Result), .sel(ALUOP));
  Multiplexer #(.select(3), .enable("false")) multiplexer_2 (
    .in0(add_1_overflow), .in1(add_1_overflow), .in2(sub_1_overflow), .in3(1'b0), .in4(1'b0), .in5(1'b0),
    .in6(1'b0), .in7(1'b0), .out(OVERFLOW), .sel(ALUOP));
  nor nor_2 (ZF, Result[0], Result[1], Result[2], Result[3]);

  // Notes on the sheet:
  //   sll
  //   srl
endmodule

module add (
  input  [3:0] A,
  input  [3:0] B,
  output [3:0] Result,
  output OVERFLOW
);

  wire adder_1_cout, adder_2_cout;

  Adder #(.width(3)) adder_1 (.a(A[2:0]), .b(B[2:0]), .out(Result[2:0]), .cout(adder_1_cout));  // open: cin
  Adder #(.width(1)) adder_2 (.a(A[3]), .b(B[3]), .out(Result[3]), .cin(adder_1_cout), .cout(adder_2_cout));
  xor xor_1 (OVERFLOW, adder_1_cout, adder_2_cout);
endmodule

module sub (
  input  [3:0] A,
  input  [3:0] B,
  output [3:0] result,
  output overflow
);

  wire [3:0] negator_1_out;

  Negator #(.width(4)) negator_1 (.in(B), .out(negator_1_out));
  add add_1 (.A(A), .B(negator_1_out), .Result(result), .OVERFLOW(overflow));
endmodule
